# Fritzing sketch Circuit (saved by Fritzing 0.9.2b)
breadboards: 1

parts:
  U1 = attiny85 [package=dip]
  J3 = female pin header, 1 pin [form="♀ (female)"]
  J4 = female pin header, 1 pin [form="♀ (female)"]
  J5 = female pin header, 1 pin [form="♀ (female)"]
  J6 = female pin header, 1 pin [form="♀ (female)"]
  J7 = female pin header, 1 pin [form="♀ (female)"]
  J9 = female pin header, 1 pin [form="♀ (female)"]
  J10 = female pin header, 1 pin [form="♀ (female)"]
  J11 = female pin header, 2 pins [form="♀ (female)"]
  J12 = female pin header, 1 pin [form="♀ (female)"]
  R1 = Resistor [tolerance=±5% resistance=47 package=THT]
  VCC1 = Battery

nets:
  N1: U1.Pin_2, J6.pin1
  N2: U1.Pin_4, J5.pin1, J12.pin1, VCC1.-
  N3: U1.Pin_5, R1.Pin_1
  N4: U1.Pin_6, J11.pin2
  N5: U1.Pin_8, J3.pin1, J7.pin1
  N6: J4.pin1, VCC1.+
  N7: J9.pin1, J11.pin1
  N8: J10.pin1, R1.Pin_0

notes:
  LED RVB
  Potentiomètre rotatif (3 pattes) avec interrupteur
  (2 pattes) au centre
